// Logisim project deucerto.circ as structural Verilog: 1 circuit, main circuit main
module main (
  input  a,
  input  b,
  input  c,
  input  d
);

  wire a_prime_b_out, ab_prime_d_prime_out, b_prime_c_out, b_prime_cd_prime_out, b_prime_d_out, b_prime_out,
       bc_prime_out, c_prime_d_out, c_prime_d_prime_out, cd_out, d_b_prime_c_out, db_out, not_1_out,
       not_2_out, not_3_out, or_1_out, or_2_out, or_3_out, or_4_out, or_5_out, or_6_out, or_7_out, or_8_out;

  not not_1 (not_1_out, a);
  not b_prime (b_prime_out, b);
  not not_2 (not_2_out, c);
  not not_3 (not_3_out, d);
  and db (db_out, d, b);
  and ab_prime_d_prime (ab_prime_d_prime_out, a, b_prime_out, not_3_out);
  or or_1 (or_1_out, not_2_out, ab_prime_d_prime_out, db_out, a_prime_b_out);
  _7_Segment_Display u_7_segment_display_1 (
    .g(or_8_out), .f(or_7_out), .a(or_1_out), .b(or_3_out), .e(or_5_out), .d(or_4_out), .c(or_2_out));  // open: dp
  and a_prime_b (a_prime_b_out, not_1_out, b);
  or or_2 (or_2_out, c, not_3_out, b_prime_out);
  and c_prime_d_prime (c_prime_d_prime_out, not_2_out, not_3_out);
  and cd (cd_out, c, d);
  or or_3 (or_3_out, b, c_prime_d_prime_out, cd_out);
  and c_prime_d (c_prime_d_out, not_2_out, d);
  and bc_prime (bc_prime_out, b, not_2_out);
  or or_4 (or_4_out, db_out, c_prime_d_out, bc_prime_out, b_prime_cd_prime_out);
  and b_prime_cd_prime (b_prime_cd_prime_out, b_prime_out, c, not_3_out);
  or or_5 (or_5_out, db_out, c_prime_d_out);
  or or_6 (or_6_out, b_prime_out, c);
  and d_b_prime_c (d_b_prime_c_out, d, or_6_out);
  or or_7 (or_7_out, not_1_out, d_b_prime_c_out, b_prime_c_out);
  and b_prime_c (b_prime_c_out, b_prime_out, c);
  and b_prime_d (b_prime_d_out, b_prime_out, d);
  or or_8 (or_8_out, not_1_out, bc_prime_out, b_prime_c_out, b_prime_d_out);

  // Notes on the sheet:
  //   a'
  //   c'
  //   d'
endmodule
