// Logisim project sistemasdigitais.circ as structural Verilog: 1 circuit, main circuit main
module main (
  input  a,
  input  b,
  input  c,
  input  d,
  output a_2,
  output b_2,
  output c_2,
  output d_2,
  output e,
  output f,
  output g
);

  wire a_prime_b_out, a_prime_out, ab_prime_d_prime_out, b_out, b_prime_c_out, b_prime_cd_prime_out,
       b_prime_d_out, b_prime_out, bc_prime_out, bd_out, c_out, c_prime_d_out, c_prime_d_prime_out,
       c_prime_out, cd_out, d_out, d_prime_out, not_1_out, not_2_out, not_3_out, not_4_out, undriven,
       undriven_2, undriven_3, undriven_4, undriven_5, undriven_6, undriven_7, undriven_8, undriven_9,
       undriven_10, undriven_11, undriven_12, undriven_13, undriven_14, undriven_15, undriven_16,
       undriven_17, undriven_18, undriven_19, undriven_20, undriven_21, undriven_22, undriven_23,
       undriven_24, undriven_25, undriven_26, undriven_27, undriven_28, undriven_29, undriven_30,
       undriven_31, undriven_32, undriven_33, undriven_34, undriven_35, undriven_36, undriven_37,
       undriven_38, undriven_39, undriven_40, undriven_41, undriven_42, undriven_43;

  not not_1 (not_1_out, b);
  not not_2 (not_2_out, a);
  not not_3 (not_3_out, d);
  not not_4 (not_4_out, c);
  and ab_prime_d_prime (ab_prime_d_prime_out, a, not_1_out, not_3_out, undriven_9);
  and bd (bd_out, d, b, undriven_20, undriven_30);
  and a_prime_b (a_prime_b_out, not_2_out, b, undriven_10, undriven_31);
  and c_prime_d_prime (c_prime_d_prime_out, not_4_out, not_3_out, undriven_21, undriven_32);
  and cd (cd_out, c, d, undriven_22, undriven_11);
  and c_prime_d (c_prime_d_out, not_4_out, d, undriven_23, undriven_33);
  and bc_prime (bc_prime_out, b, not_4_out, undriven_12, undriven_34);
  and b_prime_cd_prime (b_prime_cd_prime_out, not_1_out, c, not_3_out, undriven_35);
  and b_prime_c (b_prime_c_out, not_1_out, c, undriven_24, undriven_13);
  and b_prime_d (b_prime_d_out, not_1_out, d, undriven_25, undriven_14);
  and a_prime (a_prime_out, not_2_out, undriven_36, undriven_15, undriven_2);
  and c_prime (c_prime_out, not_4_out, undriven_37, undriven_3, undriven_4);
  and u_b (b_out, b, undriven_16, undriven_5, undriven_17);
  and u_c (c_out, c, undriven_26, undriven_38, undriven_27);
  and u_d (d_out, undriven_28, undriven_18, undriven_6, d);
  and d_prime (d_prime_out, undriven_29, undriven_39, undriven_7, not_3_out);
  and b_prime (b_prime_out, not_1_out, undriven, undriven_19, undriven_8);
  or or_1 (b_2, b_out, c_prime_d_prime_out, cd_out, undriven_40);
  or or_2 (a_2, c_prime_out, ab_prime_d_prime_out, bd_out, a_prime_b_out);
  or or_3 (c_2, c_out, d_prime_out, b_prime_out, undriven_41);
  or or_4 (d_2, bd_out, c_prime_d_out, bc_prime_out, b_prime_cd_prime_out);
  or or_5 (e, bd_out, c_prime_d_out, undriven_42, undriven_43);
  or or_6 (f, b_prime_d_out, cd_out, a_prime_out, b_prime_c_out);
  or or_7 (g, a_prime_out, bc_prime_out, b_prime_c_out, b_prime_d_out);

  // Notes on the sheet:
  //   Fórmulas booleanas
  //   a = c'+ab'd'+bd+a'b
  //   b = b+c'd'+cd
  //   c = c+d'+b'
  //   d = bd+c'd+bc'+b'cd'
  //   e = c'd+bd
  //   f = a'+db'+dc+b'c
  //   g = a'+bd+b'c+b'd
  //   Saidas
endmodule
